# Fritzing sketch SparkBot_PCB_Main (saved by Fritzing 0.9.2b)
circuit board: 4cm x 4cm

parts:
  J1 = female pin header, 12 pins [form="♀ (female)"]
  J2 = female pin header, 12 pins [form="♀ (female)"]
  P1 = Piezo Speaker
  M1 = female pin header, 3 pins [form="♀ (female)"]
  I/O = female pin header, 5 pins [form="♀ (female)"]
  RI1 = Basic Servo
  LE1 = Basic Servo
  H1 = Basic Servo
  RGB = RGB LED (com. cathode, rbg) [package="5 mm [THT]"]
  B2 = female pin header, 2 pins [form="♀ (female)"]
  B1 = female pin header, 2 pins [form="♀ (female)"]
  T1 = female pin header, 3 pins [form="♀ (female)"]
  R1 = Resistor [tolerance=±5% resistance=10k package="2512 [SMD]"]
  Battery = Battery block 9V
  R2 = Resistor [tolerance=±5% resistance=10k package="2512 [SMD]"]

nets:
  N1: J1.pin1, Battery.+
  GND: J1.pin2, RI1.gnd, LE1.gnd, H1.gnd, RGB.common_cathode, T1.pin1
  N2: J1.pin7, T1.pin2
  N3: J1.pin8, I/O.pin4
  N4: J1.pin9, I/O.pin3
  N5: J1.pin10, I/O.pin2
  N6: J1.pin11, M1.pin2
  N7: J1.pin12, P1.pin2
  VCC: J2.pin1, M1.pin3, I/O.pin5, RI1.vcc, LE1.vcc, H1.vcc, B2.pin2, B1.pin2, T1.pin3
  N8: J2.pin4, R1.Pin_0, Battery.-, R2.Pin_0
  N9: J2.pin5, B2.pin1, R2.Pin_1
  N10: J2.pin6, RGB.green_anode
  N11: J2.pin7, RGB.blue_anode
  N12: J2.pin8, RGB.red_anode
  N13: J2.pin9, B1.pin1, R1.Pin_1
  N14: J2.pin10, H1.pulse
  N15: J2.pin11, LE1.pulse
  N16: J2.pin12, RI1.pulse
  N17: P1.pin1, M1.pin1, I/O.pin1
